# Fritzing sketch GateBoard (saved by Fritzing 1.0.4)
breadboards: 1

parts:
  SparkFun_Qwiic_Pro_Micro_-_USB-C1 = SparkFun Qwiic Pro Micro - USB-C [part_number=DEV-15795]
  Mod1 = Raspberry Pi Pico
  U1 = Voltage Regulator - 5V [package="TO220 [THT]"]
  J7_-_DC_IN = Screw terminal - 2 pins [package=THT]
  Q2 = NPN-Transistor [package="TO92 [THT]"]
  Q3 = NPN-Transistor [package="TO92 [THT]"]
  Q4 = NPN-Transistor [package="TO92 [THT]"]
  Q5 = NPN-Transistor [package="TO92 [THT]"]
  R1 = Resistor [tolerance=±5% power=0.25W resistance=1k package=THT]
  R2 = Resistor [tolerance=±5% power=0.25W resistance=1k package=THT]
  R3 = Resistor [tolerance=±5% power=0.25W resistance=1k package=THT]
  R4 = Resistor [tolerance=±5% power=0.25W resistance=1k package=THT]
  V4 = DC Power [voltage=5V internal_resistance=0.1Ω]
  J3 = male pin header, 3 pins [form="♂ (male)"]
  J4 = male pin header, 3 pins [form="♂ (male)"]
  R6 = Resistor [tolerance=±5% power=0.25W resistance=4.7k package=THT]
  R7 = Resistor [tolerance=±5% power=0.25W resistance=10k package=THT]
  R8 = Resistor [tolerance=±5% power=0.25W resistance=10k package=THT]
  R9 = Resistor [tolerance=±5% power=0.25W resistance=4.7k package=THT]
  J7_-_DC_IN1 = screw terminal, 5 pins

nets:
  5V: SparkFun_Qwiic_Pro_Micro_-_USB-C1.RAW, Mod1.pin_39, U1.output_voltage, V4.V+
  GND: SparkFun_Qwiic_Pro_Micro_-_USB-C1.GND, Mod1.pin_3, Mod1.pin_8, Mod1.pin_13, Mod1.pin_18, Mod1.pin_23, Mod1.pin_28, Mod1.pin_33, Mod1.pin_38, U1.GND, J7_-_DC_IN.pin1, Q2.E, Q3.E, Q4.E, Q5.E, V4.V-, J3.pin1, J4.pin1, R7.Pin_1, R8.Pin_1, J7_-_DC_IN1.pin5
  ped: SparkFun_Qwiic_Pro_Micro_-_USB-C1.A3, R4.Pin_0
  stop: SparkFun_Qwiic_Pro_Micro_-_USB-C1.A2, R3.Pin_0
  close: SparkFun_Qwiic_Pro_Micro_-_USB-C1.A1, R2.Pin_0
  open: SparkFun_Qwiic_Pro_Micro_-_USB-C1.A0, R1.Pin_0
  N1: SparkFun_Qwiic_Pro_Micro_-_USB-C1.MOSI, J3.pin2, J4.pin2
  N2: SparkFun_Qwiic_Pro_Micro_-_USB-C1.D10, J3.pin3, J4.pin3
  N3: SparkFun_Qwiic_Pro_Micro_-_USB-C1.D2, R9.Pin_0
  N4: SparkFun_Qwiic_Pro_Micro_-_USB-C1.RX, Mod1.pin_11
  N5: SparkFun_Qwiic_Pro_Micro_-_USB-C1.TX, R6.Pin_0
  N6: Mod1.pin_12, R6.Pin_1, R7.Pin_0
  N7: Mod1.pin_37, R8.Pin_0, R9.Pin_1
  N8: U1.input_voltage, J7_-_DC_IN.pin2
  N9: Q2.B, R1.Pin_1
  N10: Q2.C, J7_-_DC_IN1.pin1
  N11: Q3.B, R2.Pin_1
  N12: Q3.C, J7_-_DC_IN1.pin2
  N13: Q4.B, R3.Pin_1
  N14: Q4.C, J7_-_DC_IN1.pin3
  N15: Q5.B, R4.Pin_1
  N16: Q5.C, J7_-_DC_IN1.pin4

custom parts:
  SparkFun Qwiic Pro Micro - USB-C: This tiny little board does all of the neat-o Arduino tricks that you're familiar with: 9x channels of 10-bit ADC, 5x PWM pins, 12x DIOs as well as hardware serial connections Rx and Tx. Running at 5V and 16MHz, this board will remind you a lot of your other favorite Arduino-compatible boards but this little guy can go just about anywhere. There is a voltage regulator on board so it can accept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
  Raspberry Pi Pico: Raspberry Pi Pico. Based around the RP2040 microcontroller the Pico is a low cost microcontroller device bringing Raspberry Pi quality, cost, and easy of use to the microcontroller space. Jan 2021, Split part in to two versions: tht (this one) and SMD. This one will drill holes for a .1 in header in pcb to allow plugging in the module as well as providing pads to solder the module to the top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
